# Fritzing sketch piano_des_rues (saved by Fritzing 0.8.0b)

parts:
  R1 = Resistor [tolerance=±5% package=axial-0.3]  # not connected
  JP1 = Header 3 [form="♀ (female)" package=screwterminal-3.5mm-3_lock.007s]  # not connected
  LPD8806_RGB_LED_Strip1 = LPD8806 RGB LED Strip  # not connected
  proto1 = Adafruit_PermaProto_1_4_Board
  Teensy_3_1 = Teensy 3.0  # not connected
  JACK1 = 2.1mm Barrel Jack with Terminal Block
  J2 = screw terminal, 3 pins
  J3 = screw terminal, 3 pins
  J4 = screw terminal, 3 pins
  J5 = screw terminal, 3 pins
  J6 = screw terminal, 3 pins
  J7 = screw terminal, 3 pins
  J8 = Screw terminal - 2 pins [package=THT]  # not connected
  J9 = Screw terminal - 2 pins [package=THT]
  J10 = Screw terminal - 2 pins [package=THT]  # not connected
  J11 = Screw terminal - 2 pins [package=THT]
  R2 = Resistor [tolerance=±5% resistance=121 package=THT]
  R3 = Resistor [tolerance=±5% resistance=220 package=THT]

nets:
  N1: proto1.connectorA1, proto1.connectorX1
  N2: proto1.connectorA4, R3.Pin_0
  N3: proto1.connectorJ11, proto1.connectorJ12
  N4: proto1.connectorJ13, R2.Pin_0
  N5: JACK1.POS, J2.pin2, J3.pin2, J4.pin2, J9.pin2, J11.pin1
  N6: JACK1.NEG, J9.pin1, J11.pin2
  N7: J2.pin1, J3.pin1, J4.pin3
  N8: J2.pin3, J3.pin3, J4.pin1, R3.Pin_1
  N9: J5.pin1, J6.pin1, J7.pin3
  N10: J5.pin2, J6.pin2, J7.pin2
  N11: J5.pin3, J6.pin3, J7.pin1, R2.Pin_1

custom parts:
  LPD8806 RGB LED Strip: Digitally addressable RGB LED strip
